# Fritzing sketch rasp00 (saved by Fritzing 0.9.3b)
breadboards: 1

parts:
  Raspberry_Pi_1 = Raspberry Pi 3 [part_number=RPI-3-V1.2]
  Part1 = HX711 Weighing Sensor Module
  LCD1 = LCD screen  # not connected

nets:
  N1: Raspberry_Pi_1.GPIO27, Part1.DO/RX
  N2: Raspberry_Pi_1.GPIO22, Part1.CK/TX
  GND: Raspberry_Pi_1.GND, Part1.GND
  5V: Raspberry_Pi_1.5V, Part1.VCC

notes:
  to load cell / scale assembly
  Grove-LCD RGB Backlight V4.0
  to GrovePi+ (mounted on RPi 3 B above)
  Raspberry Pi 3 B
  HX711 Weight Sensor
  E+
  E-
  A-
  A+
  GND
  DT
  SCK
  VCC
  Breadboard
  5V Power
  GPIO 27
  GPIO 22
  rasp00 schematic
